// Logisim project ALU.circ as structural Verilog: 1 circuit, main circuit main
module main (
  input  cs0,
  input  cs1,
  input  cs2,
  input  a3,
  input  a2,
  input  a1,
  input  a0,
  input  b3,
  input  b2,
  input  b1,
  input  b0
);

  wire n7404_1_pin2, n7404_1_pin4, n7404_1_pin6, n7404_1_pin8, n7404_1_pin10, n7404_1_pin12, n7404_2_pin10,
       n7404_2_pin11, n7408_1_pin3, n7408_1_pin6, n7408_1_pin8, n7408_1_pin11, n7408_2_pin3, n7408_2_pin6,
       n7408_2_pin8, n7408_2_pin11, n7408_3_pin1, n7408_3_pin3, n7408_3_pin5, n7408_3_pin6, n7432_1_pin2,
       n7432_1_pin5, n7432_2_pin3, n7432_2_pin11, n7486_1_pin3, n7486_1_pin6, n7486_1_pin8, n7486_1_pin11,
       n7486_2_pin3, n7486_2_pin6, n74157_1_pin4, n74157_1_pin7, n74157_1_pin9, n74157_1_pin12,
       n74157_2_pin1, n74157_2_pin4, n74157_2_pin7, n74157_2_pin9, n74157_2_pin12, n74283_1_pin1,
       n74283_1_pin2, n74283_1_pin4, n74283_1_pin6, n74283_1_pin9, n74283_1_pin10, n74283_1_pin11,
       n74283_1_pin13, n74283_1_pin15;

  _7486 #(.ShowInternalStructure("true")) u_7486_1 (
    .pin1(b2), .pin2(a2), .pin3(n7486_1_pin3), .pin4(b3), .pin5(a3), .pin6(n7486_1_pin6), .pin13(b0),
    .pin12(a0), .pin11(n7486_1_pin11), .pin10(b1), .pin9(a1), .pin8(n7486_1_pin8));
  _7404 #(.ShowInternalStructure("true")) u_7404_1 (
    .pin1(cs1), .pin2(n7404_1_pin2), .pin3(cs2), .pin4(n7404_1_pin4), .pin5(b2), .pin6(n7404_1_pin6),
    .pin13(b0), .pin12(n7404_1_pin12), .pin11(b1), .pin10(n7404_1_pin10), .pin9(b3), .pin8(n7404_1_pin8));
  _7408 #(.ShowInternalStructure("true")) u_7408_1 (
    .pin1(b2), .pin2(a2), .pin3(n7408_1_pin3), .pin4(b3), .pin5(a3), .pin6(n7408_1_pin6), .pin13(b0),
    .pin12(a0), .pin11(n7408_1_pin11), .pin10(b1), .pin9(a1), .pin8(n7408_1_pin8));
  _74157 #(.ShowInternalStructure("true")) u_74157_1 (
    .pin1(cs1), .pin2(n7408_1_pin11), .pin3(n7486_1_pin11), .pin4(n74157_1_pin4), .pin5(n7408_1_pin8),
    .pin6(n7486_1_pin8), .pin7(n74157_1_pin7), .pin14(n7408_1_pin6), .pin13(n7486_1_pin6),
    .pin12(n74157_1_pin12), .pin11(n7408_1_pin3), .pin10(n7486_1_pin3), .pin9(n74157_1_pin9));  // open: pin15
  LED led_1 (.in(n74157_1_pin12));
  LED led_2 (.in(n74157_1_pin9));
  LED led_3 (.in(n74157_1_pin7));
  LED led_4 (.in(n74283_1_pin10));
  LED led_5 (.in(n74157_1_pin4));
  _7408 #(.ShowInternalStructure("true")) u_7408_2 (
    .pin1(cs2), .pin2(n7404_1_pin2), .pin3(n7408_2_pin3), .pin4(cs1), .pin5(n7404_1_pin4),
    .pin6(n7408_2_pin6), .pin13(n7404_1_pin12), .pin12(n7408_2_pin6), .pin11(n7408_2_pin11),
    .pin10(n7408_2_pin6), .pin9(n7404_1_pin10), .pin8(n7408_2_pin8));
  _74283 #(.ShowInternalStructure("true")) u_74283_1 (
    .pin1(n74283_1_pin1), .pin2(n74283_1_pin2), .pin3(a1), .pin4(n74283_1_pin4), .pin5(a0),
    .pin6(n74283_1_pin6), .pin7(cs0), .pin15(n74283_1_pin15), .pin14(a2), .pin13(n74283_1_pin13), .pin12(a3),
    .pin11(n74283_1_pin11), .pin10(n74283_1_pin10), .pin9(n74283_1_pin9));
  LED led_6 (.in(n74283_1_pin13));
  LED led_7 (.in(n74283_1_pin1));
  LED led_8 (.in(n74283_1_pin4));
  LED led_9 (.in(n74283_1_pin11));
  LED led_10 (.in(n74283_1_pin15));
  _74157 #(.ShowInternalStructure("true")) u_74157_2 (
    .pin1(n74157_2_pin1), .pin2(n74283_1_pin4), .pin3(n74157_1_pin4), .pin4(n74157_2_pin4),
    .pin5(n74283_1_pin1), .pin6(n74157_1_pin7), .pin7(n74157_2_pin7), .pin14(n74283_1_pin10),
    .pin13(n74157_1_pin12), .pin12(n74157_2_pin12), .pin11(n74283_1_pin13), .pin10(n74157_1_pin9),
    .pin9(n74157_2_pin9));  // open: pin15
  _7432 #(.ShowInternalStructure("true")) u_7432_1 (
    .pin1(n7408_2_pin3), .pin2(n7432_1_pin2), .pin3(n74283_1_pin15), .pin4(n7408_2_pin3),
    .pin5(n7432_1_pin5), .pin6(n74283_1_pin11), .pin13(n7408_2_pin11), .pin12(n7408_2_pin3),
    .pin11(n74283_1_pin6), .pin10(n7408_2_pin8), .pin9(n7408_2_pin3), .pin8(n74283_1_pin2));
  LED led_11 (.in(n74283_1_pin2));
  LED led_12 (.in(n74283_1_pin6));
  _7408 #(.ShowInternalStructure("true")) u_7408_3 (
    .pin1(n7408_3_pin1), .pin2(n74283_1_pin9), .pin3(n7408_3_pin3), .pin4(n7408_3_pin1), .pin5(n7408_3_pin5),
    .pin6(n7408_3_pin6), .pin13(n7408_2_pin6), .pin12(n7404_1_pin6), .pin11(n7432_1_pin2),
    .pin10(n7408_2_pin6), .pin9(n7404_1_pin8), .pin8(n7432_1_pin5));
  LED led_13 (.in(n74157_2_pin12));
  LED led_14 (.in(n74157_2_pin9));
  LED led_15 (.in(n74157_2_pin7));
  _7486 #(.ShowInternalStructure("true")) u_7486_2 (
    .pin1(a3), .pin2(n74283_1_pin11), .pin3(n7486_2_pin3), .pin4(n7486_2_pin3), .pin5(n74157_2_pin12),
    .pin6(n7486_2_pin6), .pin13(cs1), .pin12(cs0), .pin11(n74157_2_pin1), .pin10(n74283_1_pin9),
    .pin9(n7486_2_pin6), .pin8(n7408_3_pin5));
  LED led_16 (.in(n74157_2_pin4));
  _7404 #(.ShowInternalStructure("true")) u_7404_2 (
    .pin13(n74157_2_pin1), .pin12(n7408_3_pin1), .pin11(n7404_2_pin11), .pin10(n7404_2_pin10));  // open: pin1, pin2, pin3, pin4, pin5, pin6, pin9, pin8
  LED led_17 (.in(n7408_3_pin3));
  LED led_18 (.in(n74157_2_pin12));
  LED led_19 (.in(n7408_3_pin6));
  LED led_20 (.in(n7404_2_pin10));
  _7432 #(.ShowInternalStructure("true")) u_7432_2 (
    .pin1(n74157_2_pin7), .pin2(n74157_2_pin4), .pin3(n7432_2_pin3), .pin13(n74157_2_pin12),
    .pin12(n74157_2_pin9), .pin11(n7432_2_pin11), .pin10(n7432_2_pin11), .pin9(n7432_2_pin3),
    .pin8(n7404_2_pin11));  // open: pin4, pin5, pin6

  // Notes on the sheet:
  //   b0'
  //   cs1'
  //   b1'
  //   b3'
  //   cs2'
  //   b2'
  //   Logical
  //   cs2. cs1'
  //   cs2'.cs1
  //        arithmatic
  //   y3
  //   y2
  //   cs2'.cs1.b0
  //   y2
  //   y1
  //   y0
  //   y1
  //   yo
  //   y3
  //   s3
  //   s2
  //   s1
  //   s0
  //   Result
  //   C
  //   Status Register
  //   S
  //   V
  //   Z
endmodule
