// Logisim project FPA3.circ as structural Verilog: 18 circuits, main circuit main
module main (
  input  [15:0] float_a,
  input  [15:0] float_b,
  output overflow,
  output underflow,
  output [15:0] sum
);

  wire align_and_add_1_adder_cout, align_and_add_1_mantissa_nonzero, align_and_add_1_sticky_bit,
       prepare_operands_1_e1_greater_final, prepare_operands_1_mantissa_op,
       prepare_operands_1_result_sign_pre;
  wire [3:0] prepare_operands_1_shift_amount_clamped;
  wire [4:0] align_and_add_1_exponent_normalized, prepare_operands_1_exp_greater,
       round_and_pack_1_exponent_final;
  wire [10:0] prepare_operands_1_significand_a, prepare_operands_1_significand_b;
  wire [13:0] align_and_add_1_adder_sum, align_and_add_1_mantissa_normalized;
  wire [15:0] round_and_pack_1_result;

  prepare_operands prepare_operands_1 (
    .float_A(float_a), .float_B(float_b), .shift_amount_clamped(prepare_operands_1_shift_amount_clamped),
    .E1_greater_final(prepare_operands_1_e1_greater_final), .exp_greater(prepare_operands_1_exp_greater),
    .mantissa_op(prepare_operands_1_mantissa_op), .result_sign_pre(prepare_operands_1_result_sign_pre),
    .significand_A(prepare_operands_1_significand_a), .significand_B(prepare_operands_1_significand_b));
  align_and_add align_and_add_1 (
    .significand_A(prepare_operands_1_significand_a), .significand_B(prepare_operands_1_significand_b),
    .shift_amount_clamped(prepare_operands_1_shift_amount_clamped),
    .mantissa_op(prepare_operands_1_mantissa_op), .E1_greater(prepare_operands_1_e1_greater_final),
    .exp_greater(prepare_operands_1_exp_greater), .adder_sum(align_and_add_1_adder_sum),
    .adder_cout(align_and_add_1_adder_cout), .sticky_bit(align_and_add_1_sticky_bit),
    .mantissa_normalized(align_and_add_1_mantissa_normalized),
    .mantissa_nonzero(align_and_add_1_mantissa_nonzero),
    .exponent_normalized(align_and_add_1_exponent_normalized));
  round_and_pack round_and_pack_1 (
    .mantissa_normalized(align_and_add_1_mantissa_normalized), .sticky_bit(align_and_add_1_sticky_bit),
    .exponent_normalized(align_and_add_1_exponent_normalized),
    .result_sign_prelim(prepare_operands_1_result_sign_pre),
    .mantissa_nonzero(align_and_add_1_mantissa_nonzero), .exponent_final(round_and_pack_1_exponent_final),
    .overflow_flag(overflow), .underflow_flag(underflow), .result(round_and_pack_1_result), .result_final(sum));

  // Notes on the sheet:
  //   float_b: initial=0x7bff
endmodule

module bigALU (
  input  [13:0] B,
  input  sub,
  input  [13:0] A,
  output [13:0] Sum,
  output Cout
);

  wire [13:0] bit_extender_1_out, xor_1_out;

  assign bit_extender_1_out = {{13{sub}}, sub};  // Bit_Extender bit_extender_1
  assign xor_1_out = B ^ bit_extender_1_out;  // XOR_Gate xor_1, 14 bits wide
  Adder #(.width(14)) adder_1 (.a(xor_1_out), .b(A), .out(Sum), .cin(sub), .cout(Cout));
endmodule

module smallALU (
  input  [4:0] B,
  input  sub,
  input  [4:0] A,
  output [4:0] Sum,
  output Cout
);

  wire [4:0] bit_extender_1_out, xor_1_out;

  assign bit_extender_1_out = {{4{sub}}, sub};  // Bit_Extender bit_extender_1
  assign xor_1_out = B ^ bit_extender_1_out;  // XOR_Gate xor_1, 5 bits wide
  Adder #(.width(5)) adder_1 (.a(xor_1_out), .b(A), .out(Sum), .cin(sub), .cout(Cout));
endmodule

module exp_comparator (
  input  [4:0] E2,
  input  [4:0] E1,
  output [4:0] difference,
  output E1_greater
);

  wire comparator_1_eq, or_1_out;
  wire [4:0] subtractor_1_out, subtractor_2_out;

  Subtractor #(.width(5)) subtractor_1 (.a(E1), .b(E2), .out(subtractor_1_out));  // open: bin, bout
  Subtractor #(.width(5)) subtractor_2 (.a(E2), .b(E1), .out(subtractor_2_out));  // open: bin, bout
  Comparator #(.mode("unsigned"), .width(5)) comparator_1 (
    .a(E1), .b(E2), .gt(E1_greater), .eq(comparator_1_eq));  // open: lt
  or or_1 (or_1_out, E1_greater, comparator_1_eq);
  Multiplexer #(.width(5)) multiplexer_1 (
    .in0(subtractor_2_out), .in1(subtractor_1_out), .out(difference), .sel(or_1_out));
endmodule

module unpack (
  input  [15:0] float,
  output sign,
  output [4:0] exponent,
  output [9:0] fraction
);


  assign exponent = float[14:10];
  assign fraction = float[9:0];
  assign sign = float[15];
endmodule

module align (
  input  [13:0] mantissa_in,
  input  [3:0] shift_amount,
  output [13:0] Mantissa_out
);

  Shifter #(.shift("lr"), .width(14)) shifter_1 (.in(mantissa_in), .\dist (shift_amount), .out(Mantissa_out));
endmodule

module sticky_calc (
  input  [13:0] mantissa_in,
  input  [3:0] shift_amount,
  output Sticky_bit
);

  wire [3:0] subtractor_1_out;
  wire [13:0] shifter_1_out;

  Subtractor #(.width(4)) subtractor_1 (
    .a(4'b1110), .b(shift_amount), .out(subtractor_1_out), .bin(1'b0));  // open: bout
  Shifter #(.width(14)) shifter_1 (.in(mantissa_in), .\dist (subtractor_1_out), .out(shifter_1_out));
  or or_1 (Sticky_bit, shifter_1_out[0], shifter_1_out[1], shifter_1_out[2], shifter_1_out[3], shifter_1_out[4], shifter_1_out[5], shifter_1_out[6], shifter_1_out[7], shifter_1_out[8], shifter_1_out[9], shifter_1_out[10], shifter_1_out[11], shifter_1_out[12], shifter_1_out[13]);
endmodule

module shift_clamp (
  input  [4:0] exp_diff,
  output [3:0] shift_amount_clamped
);

  wire comparator_1_eq, comparator_1_gt, or_1_out;

  Comparator #(.mode("unsigned"), .width(5)) comparator_1 (
    .a(exp_diff), .b(5'b01110), .gt(comparator_1_gt), .eq(comparator_1_eq));  // open: lt
  or or_1 (or_1_out, comparator_1_gt, comparator_1_eq);
  Multiplexer #(.width(4)) multiplexer_1 (
    .in0(exp_diff[3:0]), .in1(4'b1110), .out(shift_amount_clamped), .sel(or_1_out));
endmodule

module sign_logic (
  input  sign_A,
  input  sign_B,
  input  E1_greater,
  output mantissa_op,
  output result_sign
);

  xor xor_1 (mantissa_op, sign_A, sign_B);
  Multiplexer multiplexer_1 (.in0(sign_B), .in1(sign_A), .out(result_sign), .sel(E1_greater));
endmodule

module normalizer_overflow (
  input  [13:0] mantissa_result,
  input  carry_out,
  input  [4:0] exponent_in,
  output [13:0] mantissa_out,
  output [4:0] exponent_out
);

  wire [13:0] bit_extender_1_out;
  wire [14:0] shifter_1_out;

  assign bit_extender_1_out = {{13{1'b0}}, mantissa_result[0]};  // Bit_Extender bit_extender_1
  Shifter #(.shift("lr"), .width(15)) shifter_1 (
    .in({carry_out, mantissa_result}), .\dist ({3'b000, carry_out}), .out(shifter_1_out));
  smallALU smallalu_1 (.B({4'b0000, carry_out}), .sub(1'b0), .A(exponent_in), .Sum(exponent_out));  // open: Cout
  assign mantissa_out = bit_extender_1_out | shifter_1_out[13:0];  // OR_Gate or_1, 14 bits wide
endmodule

module leading_zero_detector (
  input  [13:0] mantissa_in,
  output [3:0] zero_count,
  output mantissa_nonzero
);

  wire [3:0] multiplexer_1_out, priority_encoder_1_out;

  Priority_Encoder #(.select(4)) priority_encoder_1 (
    .in0(mantissa_in[0]), .in1(mantissa_in[1]), .in2(mantissa_in[2]), .in3(mantissa_in[3]),
    .in4(mantissa_in[4]), .in5(mantissa_in[5]), .in6(mantissa_in[6]), .in7(mantissa_in[7]),
    .in8(mantissa_in[8]), .in9(mantissa_in[9]), .in10(mantissa_in[10]), .in11(mantissa_in[11]),
    .in12(mantissa_in[12]), .in13(mantissa_in[13]), .in14(1'b0), .in15(1'b0), .out(priority_encoder_1_out),
    .gs(mantissa_nonzero));  // open: en_out, en_in
  Subtractor #(.width(4)) subtractor_1 (
    .a(4'b1101), .b(multiplexer_1_out), .out(zero_count), .bin(1'b0));  // open: bout
  Multiplexer #(.width(4)) multiplexer_1 (
    .in0(4'b0000), .in1(priority_encoder_1_out), .out(multiplexer_1_out), .sel(mantissa_nonzero));
endmodule

module normalizer_underflow (
  input  [13:0] mantissa_in,
  input  [4:0] exponent_in,
  output mantissa_nonzero,
  output [13:0] mantissa_out,
  output [4:0] exponent_out
);

  wire and_1_out, comparator_1_lt;
  wire [3:0] leading_zero_detector_1_zero_count, multiplexer_3_out;
  wire [4:0] bit_extender_1_out, smallalu_1_sum, subtractor_1_out;
  wire [13:0] shifter_1_out;

  Shifter #(.width(14)) shifter_1 (.in(mantissa_in), .\dist (multiplexer_3_out), .out(shifter_1_out));
  Subtractor #(.width(5)) subtractor_1 (.a(exponent_in), .b(5'b00001), .out(subtractor_1_out));  // open: bin, bout
  leading_zero_detector leading_zero_detector_1 (
    .mantissa_in(mantissa_in), .zero_count(leading_zero_detector_1_zero_count),
    .mantissa_nonzero(mantissa_nonzero));
  Multiplexer #(.width(14)) multiplexer_1 (
    .in0({14{1'b0}}), .in1(shifter_1_out), .out(mantissa_out), .sel(mantissa_nonzero));
  smallALU smallalu_1 (
    .B({1'b0, leading_zero_detector_1_zero_count}), .sub(1'b1), .A(exponent_in), .Sum(smallalu_1_sum));  // open: Cout
  assign bit_extender_1_out = {{1{1'b0}}, leading_zero_detector_1_zero_count};  // Bit_Extender bit_extender_1
  Multiplexer #(.width(5)) multiplexer_2 (.in0({5{1'b0}}), .in1(smallalu_1_sum), .out(exponent_out), .sel(and_1_out));
  and and_1 (and_1_out, mantissa_nonzero, comparator_1_lt);
  Multiplexer #(.width(4)) multiplexer_3 (
    .in0(subtractor_1_out[3:0]), .in1(leading_zero_detector_1_zero_count), .out(multiplexer_3_out),
    .sel(and_1_out));
  Comparator #(.mode("unsigned"), .width(5)) comparator_1 (
    .a(bit_extender_1_out), .b(exponent_in), .lt(comparator_1_lt));  // open: gt, eq

  // Notes on the sheet:
  //   can_normalize
endmodule

module rounder (
  input  [13:0] mantissa_in,
  input  sticky,
  output [10:0] mantissa_rounded,
  output round_carry
);

  wire and_1_out, or_1_out, or_2_out;

  or or_1 (or_1_out, mantissa_in[0], mantissa_in[1]);
  or or_2 (or_2_out, or_1_out, mantissa_in[3]);
  and and_1 (and_1_out, or_2_out, mantissa_in[2]);
  Adder #(.width(11)) adder_1 (
    .a(mantissa_in[13:3]), .b({11{1'b0}}), .out(mantissa_rounded), .cin(and_1_out), .cout(round_carry));
endmodule

module range_check (
  input  [4:0] exponent_final,
  output overflow_flag,
  output underflow_flag
);

  wire comparator_2_eq, comparator_2_lt;

  Comparator #(.mode("unsigned"), .width(5)) comparator_1 (
    .a(exponent_final), .b(5'b11110), .gt(overflow_flag));  // open: eq, lt
  Comparator #(.mode("unsigned"), .width(5)) comparator_2 (
    .a(exponent_final), .b({5{1'b0}}), .eq(comparator_2_eq), .lt(comparator_2_lt));  // open: gt
  or or_1 (underflow_flag, comparator_2_eq, comparator_2_lt);
endmodule

module packer (
  input  sign,
  input  [4:0] exponent,
  input  [10:0] mantissa,
  output [15:0] result
);


  assign result = {sign, exponent, mantissa[9:0]};
endmodule

module prepare_operands (
  input  [15:0] float_A,
  input  [15:0] float_B,
  output [3:0] shift_amount_clamped,
  output E1_greater_final,
  output [4:0] exp_greater,
  output mantissa_op,
  output result_sign_pre,
  output [10:0] significand_A,
  output [10:0] significand_B
);

  wire and_1_out, comparator_1_eq, comparator_1_gt, comparator_2_eq, exp_comparator_1_e1_greater, or_1_out,
       unpack_1_sign, unpack_2_sign;
  wire [4:0] exp_comparator_1_difference, unpack_1_exponent, unpack_2_exponent;

  unpack unpack_1 (.float(float_A), .sign(unpack_1_sign), .exponent(unpack_1_exponent), .fraction(significand_A[9:0]));
  unpack unpack_2 (.float(float_B), .sign(unpack_2_sign), .exponent(unpack_2_exponent), .fraction(significand_B[9:0]));
  exp_comparator exp_comparator_1 (
    .E2(unpack_2_exponent), .E1(unpack_1_exponent), .difference(exp_comparator_1_difference),
    .E1_greater(exp_comparator_1_e1_greater));
  sign_logic sign_logic_1 (
    .sign_A(unpack_1_sign), .sign_B(unpack_2_sign), .E1_greater(E1_greater_final), .mantissa_op(mantissa_op),
    .result_sign(result_sign_pre));
  Multiplexer #(.width(5)) multiplexer_1 (
    .in0(unpack_2_exponent), .in1(unpack_1_exponent), .out(exp_greater), .sel(E1_greater_final));
  shift_clamp shift_clamp_1 (.exp_diff(exp_comparator_1_difference), .shift_amount_clamped(shift_amount_clamped));
  Comparator #(.mode("unsigned"), .width(11)) comparator_1 (
    .a({1'b1, significand_A[9:0]}), .b({1'b1, significand_B[9:0]}), .gt(comparator_1_gt), .eq(comparator_1_eq));  // open: lt
  Comparator #(.width(5)) comparator_2 (
    .a(exp_comparator_1_difference), .b({5{1'b0}}), .eq(comparator_2_eq));  // open: gt, lt
  or or_1 (or_1_out, comparator_1_gt, comparator_1_eq);
  and and_1 (and_1_out, comparator_2_eq, or_1_out);
  or or_2 (E1_greater_final, exp_comparator_1_e1_greater, and_1_out);

  assign significand_A[10] = 1'b1;
  assign significand_B[10] = 1'b1;
endmodule

module align_and_add (
  input  [10:0] significand_A,
  input  [10:0] significand_B,
  input  [3:0] shift_amount_clamped,
  input  mantissa_op,
  input  E1_greater,
  input  [4:0] exp_greater,
  output [13:0] adder_sum,
  output adder_cout,
  output sticky_bit,
  output [13:0] mantissa_normalized,
  output mantissa_nonzero,
  output [4:0] exponent_normalized
);

  wire and_1_out, not_1_out, or_2_out;
  wire [4:0] normalizer_overflow_1_exponent_out, normalizer_underflow_1_exponent_out;
  wire [10:0] multiplexer_1_out, multiplexer_2_out;
  wire [13:0] align_1_mantissa_out, bit_extender_1_out, normalizer_overflow_1_mantissa_out,
       normalizer_underflow_1_mantissa_out, or_1_out;

  Multiplexer #(.width(11)) multiplexer_1 (
    .in0(significand_A), .in1(significand_B), .out(multiplexer_1_out), .sel(E1_greater));
  Multiplexer #(.width(11)) multiplexer_2 (
    .in0(significand_B), .in1(significand_A), .out(multiplexer_2_out), .sel(E1_greater));
  align align_1 (
    .mantissa_in({multiplexer_1_out, 3'b000}), .shift_amount(shift_amount_clamped),
    .Mantissa_out(align_1_mantissa_out));
  not not_1 (not_1_out, mantissa_op);
  sticky_calc sticky_calc_1 (
    .mantissa_in({multiplexer_1_out, 3'b000}), .shift_amount(shift_amount_clamped), .Sticky_bit(sticky_bit));
  assign bit_extender_1_out = {{13{1'b0}}, sticky_bit};  // Bit_Extender bit_extender_1
  assign or_1_out = align_1_mantissa_out | bit_extender_1_out;  // OR_Gate or_1, 14 bits wide
  bigALU bigalu_1 (
    .B(or_1_out), .sub(mantissa_op), .A({multiplexer_2_out, 3'b000}), .Sum(adder_sum), .Cout(adder_cout));
  and and_1 (and_1_out, adder_cout, not_1_out);
  normalizer_overflow normalizer_overflow_1 (
    .mantissa_result(adder_sum), .carry_out(adder_cout), .exponent_in(exp_greater),
    .mantissa_out(normalizer_overflow_1_mantissa_out), .exponent_out(normalizer_overflow_1_exponent_out));
  normalizer_underflow normalizer_underflow_1 (
    .mantissa_in(adder_sum), .exponent_in(exp_greater), .mantissa_out(normalizer_underflow_1_mantissa_out),
    .exponent_out(normalizer_underflow_1_exponent_out));  // open: mantissa_nonzero
  or or_2 (or_2_out, adder_sum[0], adder_sum[1], adder_sum[2], adder_sum[3], adder_sum[4], adder_sum[5], adder_sum[6], adder_sum[7], adder_sum[8], adder_sum[9], adder_sum[10], adder_sum[11], adder_sum[12], adder_sum[13]);
  Multiplexer #(.width(14)) multiplexer_3 (
    .in0(normalizer_underflow_1_mantissa_out), .in1(normalizer_overflow_1_mantissa_out),
    .out(mantissa_normalized), .sel(and_1_out));
  Multiplexer #(.width(5)) multiplexer_4 (
    .in0(normalizer_underflow_1_exponent_out), .in1(normalizer_overflow_1_exponent_out),
    .out(exponent_normalized), .sel(and_1_out));
  or or_3 (mantissa_nonzero, or_2_out, and_1_out);
endmodule

module round_and_pack (
  input  [13:0] mantissa_normalized,
  input  sticky_bit,
  input  [4:0] exponent_normalized,
  input  result_sign_prelim,
  input  mantissa_nonzero,
  output [4:0] exponent_final,
  output overflow_flag,
  output underflow_flag,
  output [15:0] result,
  output [15:0] result_final
);

  wire range_check_1_underflow_flag, rounder_1_round_carry;
  wire [10:0] rounder_1_mantissa_rounded;
  wire [15:0] multiplexer_1_out, packer_1_result;

  Adder #(.width(5)) adder_1 (
    .a({5{1'b0}}), .b(exponent_normalized), .out(exponent_final), .cin(rounder_1_round_carry));  // open: cout
  packer packer_1 (.sign(result_sign_prelim), .exponent({5{1'b1}}), .mantissa({11{1'b0}}), .result(packer_1_result));
  rounder rounder_1 (
    .mantissa_in(mantissa_normalized), .sticky(sticky_bit), .mantissa_rounded(rounder_1_mantissa_rounded),
    .round_carry(rounder_1_round_carry));
  range_check range_check_1 (
    .exponent_final(exponent_final), .overflow_flag(overflow_flag),
    .underflow_flag(range_check_1_underflow_flag));
  packer packer_2 (
    .sign(result_sign_prelim), .exponent(exponent_final), .mantissa(rounder_1_mantissa_rounded),
    .result(result));
  Multiplexer #(.width(16)) multiplexer_1 (
    .in0({16{1'b0}}), .in1(result), .out(multiplexer_1_out), .sel(mantissa_nonzero));
  and and_1 (underflow_flag, range_check_1_underflow_flag, mantissa_nonzero);
  Multiplexer #(.width(16)) multiplexer_2 (
    .in0(multiplexer_1_out), .in1(packer_1_result), .out(result_final), .sel(overflow_flag));
endmodule
