// Logisim project MIPS.circ as structural Verilog: 13 circuits, main circuit main
module main (
  input  reset
);

  wire clock_1_out;
  wire [3:0] cpu_top_1_t0, cpu_top_1_t1, cpu_top_1_t2, cpu_top_1_t3, cpu_top_1_t4;
  wire [7:0] cpu_top_1_currentpc, cpu_top_1_sp;
  wire [15:0] cpu_top_1_fetched_instruction;

  Clock clock_1 (.out(clock_1_out));
  CPU_TOP cpu_top_1 (
    .clock(clock_1_out), .reset(reset), .t0(cpu_top_1_t0), .t2(cpu_top_1_t2), .t4(cpu_top_1_t4),
    .t1(cpu_top_1_t1), .t3(cpu_top_1_t3), .sp(cpu_top_1_sp), .CurrentPC(cpu_top_1_currentpc),
    .Fetched_Instruction(cpu_top_1_fetched_instruction));
  // Probe on cpu_top_1_t0
  // Probe on cpu_top_1_t1
  // Probe on cpu_top_1_t2
  // Probe on cpu_top_1_t3
  // Probe on cpu_top_1_sp
  // Probe on cpu_top_1_t4
  // Probe on cpu_top_1_currentpc
  // Probe on cpu_top_1_fetched_instruction
endmodule

module FETCH_UNIT (
  input  [7:0] BranchTarget,
  input  [7:0] JumpTarget,
  input  [1:0] PCSource,
  input  clock,
  input  reset,
  output [7:0] PCPlus1,
  output [15:0] Fetched_Instruction,
  output [7:0] CurrentPC
);

  wire [7:0] multiplexer_1_out;

  Multiplexer #(.select(2), .width(8)) multiplexer_1 (
    .in0(PCPlus1), .in1(BranchTarget), .in2(JumpTarget), .in3(PCPlus1), .out(multiplexer_1_out),
    .sel(PCSource));
  Register PC (.D(multiplexer_1_out), .en(1'b1), .clk(clock), .Q(CurrentPC), .clr(reset));
  Adder adder_1 (.a(CurrentPC), .b(8'h1), .out(PCPlus1), .cin(1'b0));  // open: cout
  ROM #(.dataWidth(16)) INSTRUCTION_MEMORY (.addr(CurrentPC), .data(Fetched_Instruction));

  // Notes on the sheet:
  //   contents of INSTRUCTION_MEMORY (hex, n*v repeats v):
  //   9021 9033 4231 4134 4125 7323 3222 121 e1a0 b415 2441 5441 d323 6241 f452 e180 7610 7620 1114 d610
  //   c330 d630 8333 e1a0 131 e100 f
endmodule

module INSTRUCTION_DECODER (
  input  [15:0] Fetched_Instruction,
  output [3:0] ImmediateOrLow,
  output [3:0] Register2,
  output [3:0] Register1,
  output [3:0] OpCode,
  output [7:0] JumpAddress
);


  assign ImmediateOrLow = Fetched_Instruction[3:0];
  assign JumpAddress = Fetched_Instruction[11:4];
  assign OpCode = Fetched_Instruction[15:12];
  assign Register1 = Fetched_Instruction[11:8];
  assign Register2 = Fetched_Instruction[7:4];
endmodule

module REGISTER_FILE (
  input  [3:0] ReadReg1,
  input  [3:0] WriteData,
  input  RegWrite,
  input  clock,
  input  [3:0] WriteReg,
  input  reset,
  input  [3:0] ReadReg2,
  output [3:0] ReadData1,
  output [3:0] ReadData2,
  output [3:0] t0,
  output [3:0] t1,
  output [3:0] t2,
  output [3:0] t3,
  output [3:0] t4
);

  wire decoder_1_out1, decoder_1_out2, decoder_1_out3, decoder_1_out4, decoder_1_out5;

  Decoder #(.select(4)) decoder_1 (
    .out1(decoder_1_out1), .out2(decoder_1_out2), .out3(decoder_1_out3), .out4(decoder_1_out4),
    .out5(decoder_1_out5), .sel(WriteReg), .en(RegWrite));  // open: out0, out6, out7, out8, out9, out10, out11, out12, out13, out14, out15
  Register #(.width(4)) t_0 (.D(WriteData), .en(decoder_1_out1), .clk(clock), .Q(t0), .clr(reset));
  Register #(.width(4)) t_1 (.D(WriteData), .en(decoder_1_out2), .clk(clock), .Q(t1), .clr(reset));
  Register #(.width(4)) t_2 (.D(WriteData), .en(decoder_1_out3), .clk(clock), .Q(t2), .clr(reset));
  Register #(.width(4)) t_3 (.D(WriteData), .en(decoder_1_out4), .clk(clock), .Q(t3), .clr(reset));
  Register #(.width(4)) t_4 (.D(WriteData), .en(decoder_1_out5), .clk(clock), .Q(t4), .clr(reset));
  Multiplexer #(.select(4), .width(4)) multiplexer_1 (
    .in0(4'b0000), .in1(t0), .in2(t1), .in3(t2), .in4(t3), .in5(t4), .in6(4'b0000), .in7(4'b0000),
    .in8(4'b0000), .in9(4'b0000), .in10(4'b0000), .in11(4'b0000), .in12(4'b0000), .in13(4'b0000),
    .in14(4'b0000), .in15(4'b0000), .out(ReadData1), .sel(ReadReg1));
  Multiplexer #(.select(4), .width(4)) multiplexer_2 (
    .in0(4'b0000), .in1(t0), .in2(t1), .in3(t2), .in4(t3), .in5(t4), .in6(4'b0000), .in7(4'b0000),
    .in8(4'b0000), .in9(4'b0000), .in10(4'b0000), .in11(4'b0000), .in12(4'b0000), .in13(4'b0000),
    .in14(4'b0000), .in15(4'b0000), .out(ReadData2), .sel(ReadReg2));

  // Other names for the same wires on the sheet: L1[3:0] = t0; L2[3:0] = t1; L3[3:0] = t2; L4[3:0] = t3; L5[3:0] = t4
endmodule

module ALU_UNIT (
  input  [3:0] OperandA,
  input  [3:0] OperandB,
  input  [2:0] ALUCtrl,
  input  [3:0] ShiftAmount,
  output [3:0] ALUResult,
  output Zero
);

  wire or_1_out;
  wire [3:0] adder_1_out, and_1_out, multiplexer_1_out, multiplexer_2_out, nor_1_out, or_2_out,
       shifter_1_out, shifter_2_out, subtractor_1_out;

  or or_1 (or_1_out, ShiftAmount[2], ShiftAmount[3]);
  Adder #(.width(4)) adder_1 (.a(OperandA), .b(OperandB), .out(adder_1_out));  // open: cin, cout
  Subtractor #(.width(4)) subtractor_1 (.a(OperandA), .b(OperandB), .out(subtractor_1_out));  // open: bin, bout
  assign and_1_out = OperandA & OperandB;  // AND_Gate and_1, 4 bits wide
  assign or_2_out = OperandA | OperandB;  // OR_Gate or_2, 4 bits wide
  assign nor_1_out = ~(OperandA | OperandB);  // NOR_Gate nor_1, 4 bits wide
  Shifter #(.width(4)) shifter_1 (.in(OperandA), .\dist (ShiftAmount[1:0]), .out(shifter_1_out));
  Shifter #(.shift("lr"), .width(4)) shifter_2 (.in(OperandA), .\dist (ShiftAmount[1:0]), .out(shifter_2_out));
  Multiplexer #(.width(4)) multiplexer_1 (.in0(shifter_1_out), .in1(4'b0000), .out(multiplexer_1_out), .sel(or_1_out));
  Multiplexer #(.width(4)) multiplexer_2 (.in0(shifter_2_out), .in1(4'b0000), .out(multiplexer_2_out), .sel(or_1_out));
  Multiplexer #(.select(3), .width(4)) multiplexer_3 (
    .in0(adder_1_out), .in1(subtractor_1_out), .in2(and_1_out), .in3(or_2_out), .in4(nor_1_out),
    .in5(multiplexer_1_out), .in6(multiplexer_2_out), .in7(4'b0000), .out(ALUResult), .sel(ALUCtrl));
  Comparator #(.width(4)) comparator_1 (.a(ALUResult), .b(4'b0000), .eq(Zero));  // open: gt, lt
endmodule

module DATA_MEMORY (
  input  [7:0] EffectiveAddress,
  input  MemWrite,
  input  MemRead,
  input  clock,
  input  [3:0] WriteData,
  output [3:0] ReadData
);

  RAM #(.asyncread("true"), .dataWidth(4)) ram_1 (
    .addr(EffectiveAddress), .we(MemWrite), .oe(MemRead), .clk(clock), .din(WriteData), .dout(ReadData));
endmodule

module ADDRESS_UNIT (
  input  [3:0] BaseAddress,
  input  [3:0] Offset,
  output [7:0] EffectiveAddress
);

  wire [7:0] bit_extender_1_out, bit_extender_2_out;

  assign bit_extender_1_out = {{4{1'b0}}, BaseAddress};  // Bit_Extender bit_extender_1
  assign bit_extender_2_out = {{4{Offset[3]}}, Offset};  // Bit_Extender bit_extender_2
  Adder adder_1 (.a(bit_extender_1_out), .b(bit_extender_2_out), .out(EffectiveAddress), .cin(1'b0));  // open: cout
endmodule

module BRANCH_JUMP_UNIT (
  input  [7:0] PCPlus1,
  input  [3:0] BranchOffset,
  input  Zero,
  input  BranchNE,
  input  Branch,
  input  Jump,
  output [7:0] BranchTarget,
  output [1:0] PCSource
);

  wire xor_1_out;
  wire [7:0] bit_extender_1_out;

  assign bit_extender_1_out = {{4{BranchOffset[3]}}, BranchOffset};  // Bit_Extender bit_extender_1
  xor xor_1 (xor_1_out, Zero, BranchNE);
  Adder adder_1 (.a(PCPlus1), .b(bit_extender_1_out), .out(BranchTarget), .cin(1'b0));  // open: cout
  and and_1 (PCSource[0], xor_1_out, Branch);

  assign PCSource[1] = Jump;
endmodule

module CONTROL_UNIT (
  input  [3:0] Opcode,
  output MemToReg,
  output DestSel,
  output [2:0] ALUCtrl,
  output ALUSrc,
  output MemWrite,
  output MemRead,
  output RegWrite,
  output Jump,
  output BranchNE,
  output Branch
);

  ROM #(.addrWidth(4), .dataWidth(12)) rom_1 (
    .addr(Opcode),
    .data({Branch, BranchNE, Jump, RegWrite, MemRead, MemWrite, ALUSrc, ALUCtrl, DestSel, MemToReg}));

  // Notes on the sheet:
  //   contents of rom_1 (hex, n*v repeats v):
  //   804 12c 124 114 102 118 10a 40 112 120 c04 106 128 181 200 10e
endmodule

module DATAPATH_SELECT (
  input  [3:0] ReadData2,
  input  [3:0] ImmediateOrLow,
  input  ALUSrc,
  input  [3:0] RegisterField2,
  input  [3:0] RegisterField3,
  input  DestSel,
  input  [3:0] ALUResult,
  input  [3:0] MemoryReadData,
  input  MemToReg,
  output [3:0] ALUOperandB,
  output [3:0] DestinationRegister,
  output [3:0] RegisterWriteData
);

  Multiplexer #(.width(4)) multiplexer_1 (.in0(ReadData2), .in1(ImmediateOrLow), .out(ALUOperandB), .sel(ALUSrc));
  Multiplexer #(.width(4)) multiplexer_2 (
    .in0(ALUResult), .in1(MemoryReadData), .out(RegisterWriteData), .sel(MemToReg));
  Multiplexer #(.width(4)) multiplexer_3 (
    .in0(RegisterField2), .in1(RegisterField3), .out(DestinationRegister), .sel(DestSel));
endmodule

module CPU_TOP (
  input  clock,
  input  reset,
  output [3:0] t0,
  output [3:0] t1,
  output [3:0] t2,
  output [3:0] t3,
  output [3:0] t4,
  output [15:0] Fetched_Instruction,
  output [7:0] CurrentPC,
  output [7:0] sp
);

  wire ALU_SRC, ALU_ZERO, BRANCH, BRANCH_NE, DEST_SEL, JUMP, MEM_READ, MEM_TO_REG, MEM_WRITE, REG_WRITE;
  wire [1:0] PC_SOURCE;
  wire [2:0] ALU_CTRL;
  wire [3:0] ALU_OPERAND_B, ALU_RESULT, DEST_REGISTER, IMM_LOW, MEMORY_READ_DATA, OPCODE, READ_DATA_1,
       READ_DATA_2, REG_FIELD_1, REG_FIELD_2, REG_WRITE_DATA;
  wire [7:0] BRANCH_TARGET, EFFECTIVE_ADDRESS, JUMP_TARGET, PC_PLUS_1;

  FETCH_UNIT fetch_unit_1 (
    .BranchTarget(BRANCH_TARGET), .JumpTarget(JUMP_TARGET), .PCSource(PC_SOURCE), .clock(clock),
    .reset(reset), .PCPlus1(PC_PLUS_1), .Fetched_Instruction(Fetched_Instruction), .CurrentPC(CurrentPC));
  CONTROL_UNIT control_unit_1 (
    .Opcode(OPCODE), .MemToReg(MEM_TO_REG), .DestSel(DEST_SEL), .ALUCtrl(ALU_CTRL), .ALUSrc(ALU_SRC),
    .MemWrite(MEM_WRITE), .MemRead(MEM_READ), .RegWrite(REG_WRITE), .Jump(JUMP), .BranchNE(BRANCH_NE),
    .Branch(BRANCH));
  INSTRUCTION_DECODER instruction_decoder_1 (
    .Fetched_Instruction(Fetched_Instruction), .ImmediateOrLow(IMM_LOW), .Register2(REG_FIELD_2),
    .Register1(REG_FIELD_1), .OpCode(OPCODE), .JumpAddress(JUMP_TARGET));
  REGISTER_FILE register_file_1 (
    .ReadReg1(REG_FIELD_1), .WriteData(REG_WRITE_DATA), .RegWrite(REG_WRITE), .clock(clock),
    .WriteReg(DEST_REGISTER), .reset(reset), .ReadReg2(REG_FIELD_2), .ReadData1(READ_DATA_1),
    .ReadData2(READ_DATA_2), .t0(t0), .t1(t1), .t2(t2), .t3(t3), .t4(t4));
  ALU_UNIT alu_unit_1 (
    .OperandA(READ_DATA_1), .OperandB(ALU_OPERAND_B), .ALUCtrl(ALU_CTRL), .ShiftAmount(IMM_LOW),
    .ALUResult(ALU_RESULT), .Zero(ALU_ZERO));
  ADDRESS_UNIT address_unit_1 (.BaseAddress(READ_DATA_1), .Offset(IMM_LOW), .EffectiveAddress(EFFECTIVE_ADDRESS));
  DATAPATH_SELECT datapath_select_1 (
    .ReadData2(READ_DATA_2), .ImmediateOrLow(IMM_LOW), .ALUSrc(ALU_SRC), .RegisterField2(REG_FIELD_2),
    .RegisterField3(IMM_LOW), .DestSel(DEST_SEL), .ALUResult(ALU_RESULT), .MemoryReadData(MEMORY_READ_DATA),
    .MemToReg(MEM_TO_REG), .ALUOperandB(ALU_OPERAND_B), .DestinationRegister(DEST_REGISTER),
    .RegisterWriteData(REG_WRITE_DATA));
  MEMORY_UNIT memory_unit_1 (
    .EffectiveAddress(EFFECTIVE_ADDRESS), .clock(clock), .WriteData(READ_DATA_2), .MemRead(MEM_READ),
    .BaseRegister(REG_FIELD_1), .MemWrite(MEM_WRITE), .reset(reset), .ReadData(MEMORY_READ_DATA), .SPValue(sp));
  BRANCH_JUMP_UNIT branch_jump_unit_1 (
    .PCPlus1(PC_PLUS_1), .BranchOffset(IMM_LOW), .Zero(ALU_ZERO), .BranchNE(BRANCH_NE), .Branch(BRANCH),
    .Jump(JUMP), .BranchTarget(BRANCH_TARGET), .PCSource(PC_SOURCE));

  // Other names for the same wires on the sheet: CLK = clock; PC[7:0] = CurrentPC
endmodule

module STACK_MEMORY (
  input  [7:0] EffectiveAddress,
  input  StackWrite,
  input  StackRead,
  input  clock,
  input  [3:0] WriteData,
  output [3:0] ReadData
);

  RAM #(.asyncread("true"), .dataWidth(4)) ram_1 (
    .addr(EffectiveAddress), .we(StackWrite), .oe(StackRead), .clk(clock), .din(WriteData), .dout(ReadData));
endmodule

module MEMORY_UNIT (
  input  [7:0] EffectiveAddress,
  input  clock,
  input  [3:0] WriteData,
  input  MemRead,
  input  [3:0] BaseRegister,
  input  MemWrite,
  input  reset,
  output [3:0] ReadData,
  output [7:0] SPValue
);

  wire comparator_1_eq, demultiplexer_1_out0, demultiplexer_1_out1, demultiplexer_2_out0,
       demultiplexer_2_out1, or_1_out;
  wire [3:0] data_memory_1_readdata, stack_memory_1_readdata;
  wire [7:0] adder_1_out, multiplexer_1_out, multiplexer_2_out, subtractor_1_out;

  Demultiplexer demultiplexer_1 (
    .out0(demultiplexer_1_out0), .out1(demultiplexer_1_out1), .in(MemRead), .sel(comparator_1_eq));
  Comparator #(.width(4)) comparator_1 (.a(BaseRegister), .b(4'b0110), .eq(comparator_1_eq));  // open: gt, lt
  Demultiplexer demultiplexer_2 (
    .out0(demultiplexer_2_out0), .out1(demultiplexer_2_out1), .in(MemWrite), .sel(comparator_1_eq));
  or or_1 (or_1_out, demultiplexer_1_out1, demultiplexer_2_out1);
  Register SP (.D(multiplexer_2_out), .en(or_1_out), .clk(clock), .Q(SPValue), .clr(reset));
  DATA_MEMORY data_memory_1 (
    .EffectiveAddress(EffectiveAddress), .MemWrite(demultiplexer_2_out0), .MemRead(demultiplexer_1_out0),
    .clock(clock), .WriteData(WriteData), .ReadData(data_memory_1_readdata));
  Subtractor subtractor_1 (.a(SPValue), .b(8'h1), .out(subtractor_1_out));  // open: bin, bout
  Adder adder_1 (.a(SPValue), .b(8'h1), .out(adder_1_out));  // open: cin, cout
  Multiplexer #(.width(8)) multiplexer_1 (
    .in0(SPValue), .in1(subtractor_1_out), .out(multiplexer_1_out), .sel(demultiplexer_2_out1));
  Multiplexer #(.width(8)) multiplexer_2 (
    .in0(subtractor_1_out), .in1(adder_1_out), .out(multiplexer_2_out), .sel(demultiplexer_1_out1));
  STACK_MEMORY stack_memory_1 (
    .EffectiveAddress(multiplexer_1_out), .StackWrite(demultiplexer_2_out1),
    .StackRead(demultiplexer_1_out1), .clock(clock), .WriteData(WriteData), .ReadData(stack_memory_1_readdata));
  Multiplexer #(.width(4)) multiplexer_3 (
    .in0(data_memory_1_readdata), .in1(stack_memory_1_readdata), .out(ReadData), .sel(comparator_1_eq));
endmodule
